# Fritzing sketch OhmMeter (saved by Fritzing 0.9.0b)
breadboards: 1

parts:
  Part1 = Arduino Uno (Rev3)
  Rk = Resistor [tolerance=±5% resistance=1k package=THT]
  Resistance_to_be_measured = Resistor [tolerance=±5% resistance=220 package=THT]

nets:
  N1: Part1.A0, Rk.Pin_0, Resistance_to_be_measured.Pin_1
  N2: Part1.5V, Resistance_to_be_measured.Pin_0
  N3: Part1.GND, Rk.Pin_1
